# Fritzing sketch radar (saved by Fritzing 0.9.4)
breadboards: 1

parts:
  Part1 = Arduino Uno (Rev3)
  Part2 = OLED Monochrome 128x64 0.96 inch [part_number=326]
  HC-SR04_Sensor_1 = HC-SR04 Ultrasonic Distance Sensor
  J1 = Basic Servo

nets:
  N1: Part1.D8, Part2.RESET
  N2: Part1.D9_PWM, Part2.DC_SA0
  N3: Part1.D11_PWM/MOSI, Part2.MOSI_SDA
  N4: Part1.D13/SCK, Part2.SCLK_SCK
  N5: Part1.D2, HC-SR04_Sensor_1.TRIG
  N6: Part1.D3_PWM, J1.pulse
  N7: Part1.D5_PWM, HC-SR04_Sensor_1.ECHO
  VCC: Part1.5V, Part2.3.3V, HC-SR04_Sensor_1.VCC, J1.vcc
  GND: Part1.GND, Part2.GND, HC-SR04_Sensor_1.GND, J1.gnd

custom parts:
  OLED Monochrome 128x64 0.96 inch: These displays are small, only about 1" diameter, but very readable due to the high contrast of an OLED display. This display is made of 128x64 individual white OLED pixels, each one is turned on or off by the controller chip. Because the display makes its own light, no backlight is required. This reduces the power required to run the OLED and is why the display has such high contrast; we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
